// Logisim project main.circ as structural Verilog: 3 circuits, main circuit main
module main (
);

  wire button_1_out;
  wire [31:0] dispalycontroller_1_out_5, dispalycontroller_1_out_6, dispalycontroller_1_out_7,
       dispalycontroller_1_out_8, dispalycontroller_1_out_9, dispalycontroller_1_out_10,
       dispalycontroller_1_out_11, dispalycontroller_1_out_12, dispalycontroller_1_out_13,
       dispalycontroller_1_out_14, dispalycontroller_1_out_15, dispalycontroller_1_out_16,
       dispalycontroller_1_out_17, dispalycontroller_1_out_18, dispalycontroller_1_out_19,
       dispalycontroller_1_out_20, dispalycontroller_1_out_21, dispalycontroller_1_out_22,
       dispalycontroller_1_out_23, dispalycontroller_1_out_24, dispalycontroller_1_out_25,
       dispalycontroller_1_out_26, dispalycontroller_1_out_27, dispalycontroller_1_out_28,
       dispalycontroller_1_out_29, dispalycontroller_1_out_30, dispalycontroller_1_out_31,
       dispalycontroller_1_out_32, dispalycontroller_1_out_33, dispalycontroller_1_out_34,
       dispalycontroller_1_out_35, dispalycontroller_1_out_36;

  Clock clock_1 ();  // open: out
  DotMatrix #(.matrixcols(32), .matrixrows(32)) dotmatrix_1 (
    .col0(dispalycontroller_1_out_5), .col1(dispalycontroller_1_out_6), .col2(dispalycontroller_1_out_7),
    .col3(dispalycontroller_1_out_8), .col4(dispalycontroller_1_out_9), .col5(dispalycontroller_1_out_10),
    .col6(dispalycontroller_1_out_11), .col7(dispalycontroller_1_out_12), .col8(dispalycontroller_1_out_13),
    .col9(dispalycontroller_1_out_14), .col10(dispalycontroller_1_out_15),
    .col11(dispalycontroller_1_out_16), .col12(dispalycontroller_1_out_17),
    .col13(dispalycontroller_1_out_18), .col14(dispalycontroller_1_out_19),
    .col15(dispalycontroller_1_out_20), .col16(dispalycontroller_1_out_21),
    .col17(dispalycontroller_1_out_22), .col18(dispalycontroller_1_out_23),
    .col19(dispalycontroller_1_out_24), .col20(dispalycontroller_1_out_25),
    .col21(dispalycontroller_1_out_26), .col22(dispalycontroller_1_out_27),
    .col23(dispalycontroller_1_out_28), .col24(dispalycontroller_1_out_29),
    .col25(dispalycontroller_1_out_30), .col26(dispalycontroller_1_out_31),
    .col27(dispalycontroller_1_out_32), .col28(dispalycontroller_1_out_33),
    .col29(dispalycontroller_1_out_34), .col30(dispalycontroller_1_out_35), .col31(dispalycontroller_1_out_36));
  dispalyController dispalycontroller_1 (
    .clock(button_1_out), .out_5(dispalycontroller_1_out_5), .out_17(dispalycontroller_1_out_17),
    .out_29(dispalycontroller_1_out_29), .out_6(dispalycontroller_1_out_6),
    .out_18(dispalycontroller_1_out_18), .out_30(dispalycontroller_1_out_30),
    .out_7(dispalycontroller_1_out_7), .out_19(dispalycontroller_1_out_19),
    .out_31(dispalycontroller_1_out_31), .out_8(dispalycontroller_1_out_8),
    .out_20(dispalycontroller_1_out_20), .out_32(dispalycontroller_1_out_32),
    .out_9(dispalycontroller_1_out_9), .out_21(dispalycontroller_1_out_21),
    .out_33(dispalycontroller_1_out_33), .out_10(dispalycontroller_1_out_10),
    .out_22(dispalycontroller_1_out_22), .out_34(dispalycontroller_1_out_34),
    .out_11(dispalycontroller_1_out_11), .out_23(dispalycontroller_1_out_23),
    .out_35(dispalycontroller_1_out_35), .out_12(dispalycontroller_1_out_12),
    .out_24(dispalycontroller_1_out_24), .out_36(dispalycontroller_1_out_36),
    .out_13(dispalycontroller_1_out_13), .out_25(dispalycontroller_1_out_25),
    .out_14(dispalycontroller_1_out_14), .out_26(dispalycontroller_1_out_26),
    .out_15(dispalycontroller_1_out_15), .out_27(dispalycontroller_1_out_27),
    .out_16(dispalycontroller_1_out_16), .out_28(dispalycontroller_1_out_28));  // open: column, picture, selectCol
  Button button_1 (.out(button_1_out));
  Button button_2 ();  // open: out
  Button button_3 ();  // open: out
  Button button_4 ();  // open: out
  Button button_5 ();  // open: out
endmodule

module dispalyController (
  input  clock,
  input  [4:0] column,
  input  [31:0] picture,
  output [31:0] selectCol,
  output [31:0] out_5,
  output [31:0] out_6,
  output [31:0] out_7,
  output [31:0] out_8,
  output [31:0] out_9,
  output [31:0] out_10,
  output [31:0] out_11,
  output [31:0] out_12,
  output [31:0] out_13,
  output [31:0] out_14,
  output [31:0] out_15,
  output [31:0] out_16,
  output [31:0] out_17,
  output [31:0] out_18,
  output [31:0] out_19,
  output [31:0] out_20,
  output [31:0] out_21,
  output [31:0] out_22,
  output [31:0] out_23,
  output [31:0] out_24,
  output [31:0] out_25,
  output [31:0] out_26,
  output [31:0] out_27,
  output [31:0] out_28,
  output [31:0] out_29,
  output [31:0] out_30,
  output [31:0] out_31,
  output [31:0] out_32,
  output [31:0] out_33,
  output [31:0] out_34,
  output [31:0] out_35,
  output [31:0] out_36
);

  wire [31:0] s0, s1, s2, s3, s4, s5, s6, s7, s8, s9, s10, s11, s12, s13, s14, s15, s16, s17, s18, s19, s20,
       s21, s22, s23, s24, s25, s26, s27, s28, s29, s30, s31;

  Register #(.width(32), .trigger("falling")) register_1 (.D(s0), .Q(out_5), .clk(clock));  // open: en, clr
  Register #(.width(32), .trigger("falling")) register_2 (.D(s12), .Q(out_17), .clk(clock));  // open: en, clr
  Register #(.width(32), .trigger("falling")) register_3 (.D(s24), .Q(out_29), .clk(clock));  // open: en, clr
  Register #(.width(32), .trigger("falling")) register_4 (.D(s1), .Q(out_6), .clk(clock));  // open: en, clr
  Register #(.width(32), .trigger("falling")) register_5 (.D(s13), .Q(out_18), .clk(clock));  // open: en, clr
  Register #(.width(32), .trigger("falling")) register_6 (.D(s25), .Q(out_30), .clk(clock));  // open: en, clr
  Register #(.width(32), .trigger("falling")) register_7 (.D(s2), .Q(out_7), .clk(clock));  // open: en, clr
  Register #(.width(32), .trigger("falling")) register_8 (.D(s14), .Q(out_19), .clk(clock));  // open: en, clr
  Register #(.width(32), .trigger("falling")) register_9 (.D(s26), .Q(out_31), .clk(clock));  // open: en, clr
  Demultiplexer #(.select(5), .width(32), .enable("false")) demultiplexer_1 (
    .out0(s0), .out1(s1), .out2(s2), .out3(s3), .out4(s4), .out5(s5), .out6(s6), .out7(s7), .out8(s8),
    .out9(s9), .out10(s10), .out11(s11), .out12(s12), .out13(s13), .out14(s14), .out15(s15), .out16(s16),
    .out17(s17), .out18(s18), .out19(s19), .out20(s20), .out21(s21), .out22(s22), .out23(s23), .out24(s24),
    .out25(s25), .out26(s26), .out27(s27), .out28(s28), .out29(s29), .out30(s30), .out31(s31), .in(picture),
    .sel(column));
  Register #(.width(32), .trigger("falling")) register_10 (.D(s3), .Q(out_8), .clk(clock));  // open: en, clr
  Register #(.width(32), .trigger("falling")) register_11 (.D(s15), .Q(out_20), .clk(clock));  // open: en, clr
  Register #(.width(32), .trigger("falling")) register_12 (.D(s27), .Q(out_32), .clk(clock));  // open: en, clr
  Register #(.width(32), .trigger("falling")) register_13 (.D(s4), .Q(out_9), .clk(clock));  // open: en, clr
  Register #(.width(32), .trigger("falling")) register_14 (.D(s16), .Q(out_21), .clk(clock));  // open: en, clr
  Register #(.width(32), .trigger("falling")) register_15 (.D(s28), .Q(out_33), .clk(clock));  // open: en, clr
  Register #(.width(32), .trigger("falling")) register_16 (.D(s5), .Q(out_10), .clk(clock));  // open: en, clr
  Register #(.width(32), .trigger("falling")) register_17 (.D(s17), .Q(out_22), .clk(clock));  // open: en, clr
  Register #(.width(32), .trigger("falling")) register_18 (.D(s29), .Q(out_34));  // open: en, clk, clr
  Register #(.width(32), .trigger("falling")) register_19 (.D(s6), .Q(out_11), .clk(clock));  // open: en, clr
  Register #(.width(32), .trigger("falling")) register_20 (.D(s18), .Q(out_23), .clk(clock));  // open: en, clr
  Register #(.width(32), .trigger("falling")) register_21 (.D(s30), .Q(out_35), .clk(clock));  // open: en, clr
  Register #(.width(32), .trigger("falling")) register_22 (.D(s7), .Q(out_12), .clk(clock));  // open: en, clr
  Register #(.width(32), .trigger("falling")) register_23 (.D(s19), .Q(out_24), .clk(clock));  // open: en, clr
  Register #(.width(32), .trigger("falling")) register_24 (.D(s31), .Q(out_36), .clk(clock));  // open: en, clr
  Register #(.width(32), .trigger("falling")) register_25 (.D(s8), .Q(out_13), .clk(clock));  // open: en, clr
  Register #(.width(32), .trigger("falling")) register_26 (.D(s20), .Q(out_25), .clk(clock));  // open: en, clr
  Register #(.width(32), .trigger("falling")) register_27 (.D(s9), .Q(out_14), .clk(clock));  // open: en, clr
  Register #(.width(32), .trigger("falling")) register_28 (.D(s21), .Q(out_26));  // open: en, clk, clr
  Register #(.width(32), .trigger("falling")) register_29 (.D(s10), .Q(out_15), .clk(clock));  // open: en, clr
  Register #(.width(32), .trigger("falling")) register_30 (.D(s22), .Q(out_27), .clk(clock));  // open: en, clr
  Multiplexer #(.select(5), .width(32), .enable("false")) multiplexer_1 (
    .in0(out_5), .in1(out_6), .in2(out_7), .in3(out_8), .in4(out_9), .in5(out_10), .in6(out_11),
    .in7(out_12), .in8(out_13), .in9(out_14), .in10(out_15), .in11(out_16), .in12(out_17), .in13(out_18),
    .in14(out_19), .in15(out_20), .in16(out_21), .in17(out_22), .in18(out_23), .in19(out_24), .in20(out_25),
    .in21(out_26), .in22(out_27), .in23(out_28), .in24(out_29), .in25(out_30), .in26(out_31), .in27(out_32),
    .in28(out_33), .in29(out_34), .in30(out_35), .in31(out_36), .out(selectCol), .sel(column));
  Register #(.width(32), .trigger("falling")) register_31 (.D(s11), .Q(out_16), .clk(clock));  // open: en, clr
  Register #(.width(32), .trigger("falling")) register_32 (.D(s23), .Q(out_28), .clk(clock));  // open: en, clr

  // Other names for the same wires on the sheet: clk = clock; col[4:0] = column; o0[31:0] = out_5; o1[31:0] = out_6;
  //   o2[31:0] = out_7; o3[31:0] = out_8; o4[31:0] = out_9; o5[31:0] = out_10; o6[31:0] = out_11; o7[31:0] = out_12;
  //   o8[31:0] = out_13; o9[31:0] = out_14; o10[31:0] = out_15; o11[31:0] = out_16; o12[31:0] = out_17;
  //   o13[31:0] = out_18; o14[31:0] = out_19; o15[31:0] = out_20; o16[31:0] = out_21; o17[31:0] = out_22;
  //   o18[31:0] = out_23; o19[31:0] = out_24; o20[31:0] = out_25; o21[31:0] = out_26; o22[31:0] = out_27;
  //   o23[31:0] = out_28; o24[31:0] = out_29; o25[31:0] = out_30; o26[31:0] = out_31; o27[31:0] = out_32;
  //   o28[31:0] = out_33; o29[31:0] = out_34; o30[31:0] = out_35; o31[31:0] = out_36
endmodule

module tankObjectPlayer (
  input  clock,
  input  [1:0] way,
  input  shot
);

  Register #(.width(32), .trigger("falling")) col1 ();  // open: D, en, Q, clk, clr
  Register #(.width(32), .trigger("falling")) col2 ();  // open: D, en, Q, clk, clr
  Register #(.width(32), .trigger("falling")) col3 ();  // open: D, en, Q, clk, clr
  Register #(.width(5), .trigger("falling")) X ();  // open: D, en, Q, clk, clr
  Register #(.width(5), .trigger("falling")) Y ();  // open: D, en, Q, clk, clr
  Register #(.width(2)) position ();  // open: D, en, Q, clk, clr

  // Other names for the same wires on the sheet: clk = clock
endmodule
